// Logisim project imm_gen.circ as structural Verilog: 1 circuit, main circuit imm_gen
module imm_gen (
  input  [31:0] inst,
  input  [2:0] ImmSel,
  output [31:0] imm
);

  Multiplexer #(.enable("false"), .width(21)) multiplexer_1 (
    .in0({21{1'b0}}), .in1({21{1'b1}}), .out(imm[31:11]), .sel(inst[31]));

  assign imm[10:0] = inst[30:20];

  // Notes on the sheet:
  //   INPUTS to your circuit
  //   DON'T CHANGE THE LOCATIONS OF THE INPUTS AND OUTPUTS!
  //   OUTPUT from your circuit
endmodule
